# Fritzing sketch SensorBoard (saved by Fritzing 0.9.2b)
circuit board: 3.0736cm x 3.11901cm
breadboards: 1

parts:
  R2 = Resistor [tolerance=±5% resistance=100k package=THT]
  FR = Photocell (LDR) [package=THT]
  NTC = Temperature Sensor (Thermistor) [thermistor_type=NTC package=THT]
  J2 = female pin header, 2 pins [form="♀ (female)"]
  J1 = female pin header, 6 pins [form="♀ (female)"]
  LED1 = smd LED [color="Red (635nm)" package="1206 [SMD]"]
  R4 = Resistor [tolerance=±5% resistance=2.2k package=THT]
  R3 = Resistor [tolerance=±5% resistance=2.2k package=THT]
  R1 = Resistor [tolerance=±0.25% resistance=15k package=THT]
  J5 = female pin header, 4 pins [form="♀ (female)"]

nets:
  N1: R2.Pin_0, J1.pin2, R4.Pin_0, R3.Pin_0, R1.Pin_0, J5.pin1
  N2: R2.Pin_1, FR.pin_1, J1.pin4
  N3: FR.pin_0, NTC.pin_0, J2.pin1, J1.pin1, LED1.cathode, J5.pin2
  N4: NTC.pin_1, J1.pin3, R1.Pin_1
  N5: J2.pin2, J1.pin6, R3.Pin_1
  N6: J1.pin5, J5.pin4
  N7: LED1.anode, R4.Pin_1

notes:
  soil sensor
  pump
  arduino
  components on breadboard side
